# Fritzing sketch wirings (saved by Fritzing 0.9.2b)
breadboards: 1
perfboards: 2

parts:
  Part1 = RFID-RC522-v2
  U1 = NodeMCU V1.0
  LED1 = RGB LED (com. cathode, rgb) [package="5 mm [THT]"]
  Q3 = TRANSISTOR_NPN [package=to-92-ammo]
  R1 = Resistor [tolerance=±5% resistance=1k package="0402 [SMD]"]
  R2 = Resistor [tolerance=±5% resistance=1k package="0402 [SMD]"]
  R3 = Resistor [tolerance=±5% resistance=1k package="0402 [SMD]"]
  X1 = USB Connectors [package=usb-a-s-silk-female]
  R4 = Resistor [tolerance=±5% resistance=220 package="0402 [SMD]"]
  R5 = Resistor [tolerance=±5% resistance=220 package="0402 [SMD]"]
  R6 = Resistor [tolerance=±5% resistance=220 package="0402 [SMD]"]
  Q1 = TRANSISTOR_NPN [package=to-92-ammo]
  Q2 = TRANSISTOR_NPN [package=to-92-ammo]
  U2 = NodeMCU V1.0  # not connected
  LED2 = RGB LED (com. cathode, rgb) [package="5 mm [THT]"]
  JP1 = M16 [package=1x16_machine-pin-header_lock.004]  # not connected
  JP2 = M16 [package=1x16_machine-pin-header_lock.004]  # not connected
  JP3 = Header 8 [package=1x08_smd]  # not connected
  R7 = Resistor [tolerance=±5% resistance=100 package="0402 [SMD]"]
  R8 = Resistor [tolerance=±5% resistance=180 package="0402 [SMD]"]
  R9 = Resistor [tolerance=±5% resistance=180 package="0402 [SMD]"]
  Part2 = RFID-RC522-v2  # not connected
  R10 = Resistor [tolerance=±5% resistance=100 package="0402 [SMD]"]
  R11 = Resistor [tolerance=±5% resistance=180 package="0402 [SMD]"]
  R12 = Resistor [tolerance=±5% resistance=180 package="0402 [SMD]"]
  Q4 = TRANSISTOR_NPN [package=to-92-ammo]  # not connected
  Q5 = TRANSISTOR_NPN [package=to-92-ammo]  # not connected
  Q6 = TRANSISTOR_NPN [package=to-92-ammo]
  R13 = Resistor [tolerance=±5% resistance=1k package="0402 [SMD]"]
  R14 = Resistor [tolerance=±5% resistance=1k package="0402 [SMD]"]  # not connected
  R15 = Resistor [tolerance=±5% resistance=1k package="0402 [SMD]"]  # not connected

nets:
  N1: Part1.SCK, U1.D5
  N2: Part1.MOSI, U1.D7
  N3: Part1.MISO, U1.D6
  GND: Part1.GND, U1.GND, LED1.common_cathode, X1.GND
  N4: Part1.RST, U1.D1
  N5: U1.D2, R1.Pin_0
  N6: U1.D3, R2.Pin_0
  N7: U1.D8, R3.Pin_0
  N8: LED1.red_anode, Q2.E
  N9: LED1.green_anode, Q3.E
  N10: LED1.blue_anode, Q1.E
  N11: Q3.B, R3.Pin_1
  N12: Q3.C, R4.Pin_1
  N13: R1.Pin_1, Q1.B
  N14: R2.Pin_1, Q2.B
  N15: X1.VBUS, R4.Pin_0, R5.Pin_0, R6.Pin_0
  N16: R5.Pin_1, Q2.C
  N17: R6.Pin_1, Q1.C
  N18: LED2.red_anode, R7.Pin_0, R10.Pin_0
  N19: LED2.green_anode, R8.Pin_0
  N20: LED2.blue_anode, R9.Pin_0, R11.Pin_0
  N21: R7.Pin_1, R10.Pin_1, Q6.E
  N22: R8.Pin_1, R12.Pin_1
  N23: R9.Pin_1, R11.Pin_1
  N24: Q6.B, R13.Pin_0

notes:
  see pinout
  http://www.cnx-software.com/wp-content/uploads/2015/04/NodeMCU_Pinout.png
  when programming use gpio numbers (not the nodmcu numbers)

custom parts:
  RFID-RC522-v2: A simple China made RFID-RC522 Reader; do check the pin labels, as this is a MFRC522 based clone.
  NodeMCU V1.0: ESP9266 based NodeMCU
